# Fritzing sketch test1 (saved by Fritzing 0.9.6b)
breadboards: 1

parts:
  IC1 = IC, DIP package, 14 pins [chip_label=74HC00]
  IC2 = IC, DIP package, 14 pins [chip_label=74HC20]

nets:
  N1: IC1.pin1, IC1.pin11
  N2: IC1.pin2, IC1.pin9
  N3: IC1.pin3, IC1.pin4
  N4: IC1.pin5, IC2.pin8
  N5: IC1.pin7, IC2.pin7
  N6: IC1.pin8, IC2.pin9
  N7: IC1.pin10, IC1.pin14, IC2.pin10, IC2.pin14
  N8: IC1.pin12, IC2.pin13
  N9: IC1.pin13, IC2.pin12
