# Fritzing sketch test2 (saved by Fritzing 0.9.6b)
breadboards: 1

parts:
  IC1 = IC, DIP package, 14 pins [chip_label=74HC00]
  IC2 = IC, DIP package, 14 pins [chip_label=74HC20]

nets:
  N1: IC1.pin1, IC2.pin8
  N2: IC1.pin2, IC2.pin6
  N3: IC1.pin6, IC2.pin2, IC2.pin9
  N4: IC1.pin7, IC2.pin7
  N5: IC1.pin8, IC2.pin1
  N6: IC1.pin9, IC2.pin12
  N7: IC1.pin10, IC1.pin14, IC2.pin10, IC2.pin14
  N8: IC1.pin11, IC2.pin13
  N9: IC1.pin12, IC2.pin5
  N10: IC1.pin13, IC2.pin4
