// Digital circuit 二进制iBCD2<x<7.dig as structural Verilog
module \二进制iBCD2_x_7  (
  input  B3,
  input  B2,
  input  B1,
  input  B0,
  output Y
);

  wire dipswitch_1_out, dipswitch_2_out, dipswitch_3_out, nand_1_out, nand_2_out, nand_3_out, nand_4_out,
       nand_5_out;

  DipSwitch #(.dipDefault("true")) dipswitch_1 (.out(dipswitch_1_out));
  DipSwitch #(.dipDefault("true")) dipswitch_2 (.out(dipswitch_2_out));
  nand nand_1 (nand_1_out, dipswitch_1_out, B3);
  nand nand_2 (nand_2_out, dipswitch_2_out, B2);
  nand nand_3 (nand_3_out, B1, B0);
  DipSwitch #(.dipDefault("true")) dipswitch_3 (.out(dipswitch_3_out));
  nand nand_4 (nand_4_out, dipswitch_3_out, nand_1_out, B2, nand_3_out);
  nand nand_5 (nand_5_out, nand_1_out, nand_2_out, B1, B0);
  nand nand_6 (Y, nand_4_out, nand_5_out);
endmodule
