// Digital circuit 发电机控制电路.dig as structural Verilog
module \发电机控制电路  (
  input  C,
  input  B,
  input  A,
  output X,
  output Y
);

  wire _7400_1_pin3, _7420_1_pin6, _74138_1_pin7, _74138_1_pin9, _74138_1_pin10, _74138_1_pin11,
       _74138_1_pin12, _74138_1_pin13, _74138_1_pin14;

  _74138 _74138_1 (
    .pin1(C), .pin2(B), .pin3(A), .pin4(1'b0), .pin5(1'b0), .pin6(1'b1), .pin7(_74138_1_pin7), .pin8(1'b0),
    .pin9(_74138_1_pin9), .pin10(_74138_1_pin10), .pin11(_74138_1_pin11), .pin12(_74138_1_pin12),
    .pin13(_74138_1_pin13), .pin14(_74138_1_pin14), .pin16(1'b1));  // open: pin15
  _7420 _7420_1 (
    .pin1(_74138_1_pin14), .pin2(_74138_1_pin13), .pin4(_74138_1_pin12), .pin5(_74138_1_pin11),
    .pin6(_7420_1_pin6), .pin7(1'b0), .pin8(Y), .pin9(_74138_1_pin7), .pin10(_74138_1_pin9),
    .pin12(_74138_1_pin10), .pin13(1'b1), .pin14(1'b1));  // open: pin3, pin11
  _7400 _7400_1 (
    .pin1(1'b1), .pin2(_7420_1_pin6), .pin3(_7400_1_pin3), .pin4(_7400_1_pin3), .pin5(_74138_1_pin7),
    .pin6(X), .pin7(1'b0), .pin9(1'b0), .pin10(1'b0), .pin12(1'b0), .pin13(1'b0), .pin14(1'b1));  // open: pin8, pin11
endmodule
