// Digital circuit 血型匹配电路.dig as structural Verilog
module \血型匹配电路  (
  input  R0,
  input  R1,
  input  D0,
  input  D1,
  output Y
);

  wire _74151_1_pin2, dipswitch_1_out, nand_1_out;

  DipSwitch dipswitch_1 (.out(dipswitch_1_out));
  nand nand_1 (nand_1_out, _74151_1_pin2, D1);
  _74151 _74151_1 (
    .pin1(dipswitch_1_out), .pin2(_74151_1_pin2), .pin3(dipswitch_1_out), .pin4(nand_1_out), .pin5(Y),
    .pin7(dipswitch_1_out), .pin8(1'b0), .pin9(R0), .pin10(R1), .pin11(D0), .pin12(_74151_1_pin2),
    .pin13(_74151_1_pin2), .pin14(nand_1_out), .pin15(nand_1_out), .pin16(1'b1));  // open: pin6
  DipSwitch #(.dipDefault("true")) dipswitch_2 (.out(_74151_1_pin2));
endmodule
